# Fritzing sketch esp-motor-tester (saved by Fritzing 0.9.6b)

parts:
  WeMos_D1_Mini1 = WeMos D1 Mini
  part = YOUMILE Slot Typ IR Optokopplermodul LM393
  L298N2 = L298N DC motor driver
  M3 = DC Motor  # not connected
  VCC1 = Battery
  R2 = Resistor [tolerance=±5% power=0.25 resistance=10k package=THT]
  R1 = Resistor [tolerance=±5% power=0.25 resistance=100k package=THT]

nets:
  3V3: WeMos_D1_Mini1.3V3, part.VCC
  5V: WeMos_D1_Mini1.5V, L298N2.5V
  N1: WeMos_D1_Mini1.A0, R2.Pin_0, R1.Pin_1
  N2: WeMos_D1_Mini1.D1, L298N2.IN3
  N3: WeMos_D1_Mini1.D2, L298N2.IN4
  N4: WeMos_D1_Mini1.D3, L298N2.ENB
  N5: WeMos_D1_Mini1.D4, part.D0
  GND: WeMos_D1_Mini1.G, part.GND, L298N2.GND, VCC1.-, R2.Pin_1
  N6: L298N2.12V, VCC1.+, R1.Pin_0

custom parts:
  YOUMILE Slot Typ IR Optokopplermodul LM393: Optoisolator module with digital and analog output.
  L298N DC motor driver: 2x DC motor driver with 78M05 positive voltage regulator (7..35 V) L298N: max 46 V, 2 A Set 5 V Enable jumper to enable 5 V regultor (needed for the L298N) and +5 V output at screw terminal or supply external +5 V at screw terminal Set ENA and/or ENB to +5 V to enable motor permanently or supply ENA and/or ENB with PWM signal IN1 and IN2 set rotation directory for motor A (OUT1/OUT2) IN2 and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
